// Logisim project 0_Main Circuit.circ as structural Verilog: 1 circuit, main circuit main
module main (
);

  wire button_1_out, clock_1_out, Forward_RsD, Forward_RtD, main_1_clear_execute, main_1_stall_fetch_decode,
       main_3_out_4, main_4_alusrc, main_4_branch, main_4_jtopc, main_4_memtoreg, main_4_memwrite,
       main_4_op_3, main_4_regdst, main_4_regwrite, main_6_rd1_2, main_6_rd1_4, main_6_rd1_5, main_6_rd1_8,
       main_6_rd1_9, main_6_rd1_10, main_6_regwrite_2, main_8_rd1_2, main_8_rd1_3, main_8_rd1_4,
       main_8_rd1_6, main_10_rd1, main_10_regwrite_2;
  wire [1:0] main_1_forward_rs, main_1_forward_rt;
  wire [2:0] main_4_op_2_0, main_6_rd1_7;
  wire [3:0] adder_1_out;
  wire [4:0] main_2_instruction_2_2, main_6_rd_11_15, main_6_rs_21_25, main_6_rt_16_20, main_8_write_add_2,
       main_10_write_add_2, multiplexer_5_out;
  wire [5:0] main_2_instruction_2, main_2_instruction_2_4;
  wire [25:11] main_2_instruction_2_3;
  wire [27:0] adder_1_out_2, bit_extender_2_out, main_6_imm_0_25_2, main_8_jump_add_2, shifter_2_out;
  wire [31:0] adder_2_out, ALU_result, bit_extender_1_out, main_2_pc_4_2, main_5_rd1, main_5_rd1_2,
       main_6_imm_0_15_2, main_6_rd1_3, main_6_rd2_2, main_7_alu_result, main_8_rt_data_2,
       main_10_alu_result_2, main_10_read_data_2, MemtoRegM, multiplexer_1_out, multiplexer_2_out,
       multiplexer_3_out, multiplexer_4_out, multiplexer_6_out, multiplexer_7_out, multiplexer_8_out,
       register_1_q, rom_1_data, shifter_1_out, WB_data;

  Clock clock_1 (.out(clock_1_out));
  Multiplexer #(.width(32)) multiplexer_1 (
    .in0({adder_1_out, adder_1_out_2}), .in1(adder_2_out), .out(multiplexer_1_out), .sel(main_3_out_4));  // open: en
  Multiplexer #(.width(32)) multiplexer_2 (
    .in0(multiplexer_1_out), .in1({adder_1_out, main_8_jump_add_2}), .out(multiplexer_2_out),
    .sel(main_8_rd1_2));  // open: en
  Register #(.width(32)) register_1 (
    .D(multiplexer_2_out), .en(main_1_stall_fetch_decode), .Q(register_1_q), .clk(clock_1_out),
    .clr(button_1_out));
  Button button_1 (.out(button_1_out));
  LED led_1 (.in(clock_1_out));
  Adder #(.width(32)) adder_1 (.a(register_1_q), .b(32'h4), .out({adder_1_out, adder_1_out_2}));  // open: cin, cout
  ROM #(.addrWidth(24), .dataWidth(32)) rom_1 (.addr(register_1_q[25:2]), .data(rom_1_data));  // open: sel
  Hazard_Stalling_DataForwarding_main main_1 (
    .rs_Decode(main_2_instruction_2_3[25:21]), .rt_Execute(main_6_rt_16_20),
    .rt_Decode(main_2_instruction_2_3[20:16]), .MemtoReg_Execute(main_6_rd1_4),
    .Stall_Fetch_Decode(main_1_stall_fetch_decode), .RegWrite_WriteBack(main_10_regwrite_2),
    .rs_Execute(main_6_rs_21_25), .RegWrite_Memory(main_8_rd1_6), .WriteReg_Memory(main_8_write_add_2),
    .Forward_rs(main_1_forward_rs), .WriteReg_WriteBack(main_10_write_add_2), .Forward_rt(main_1_forward_rt),
    .Forward_RsD(Forward_RsD), .CLK(clock_1_out), .Clear_Execute(main_1_clear_execute),
    .Forward_RtD(Forward_RtD), .MemtoRegM(main_8_rd1_3));
  _5_1_Register_main main_2 (
    .CLK(clock_1_out), .PC_4({adder_1_out, adder_1_out_2}),
    .Instruction_2({main_2_instruction_2_4, main_2_instruction_2_3, main_2_instruction_2_2, main_2_instruction_2}),
    .PC_4_2(main_2_pc_4_2), .Instruction(rom_1_data), .EN(main_1_stall_fetch_decode));
  // Probe on WB_data
  Early_Branch_main main_3 (
    .in_1(multiplexer_4_out), .in_2(main_4_branch), .in_3(multiplexer_3_out), .out_4(main_3_out_4));
  // Probe on main_2_instruction_2_3[25:21]
  // Probe on main_2_instruction_2_3[20:16]
  // Probe on main_10_write_add_2
  assign bit_extender_1_out = {{16{main_2_instruction_2_3[15]}}, {main_2_instruction_2_3[15:11], main_2_instruction_2_2, main_2_instruction_2}};  // Bit_Extender bit_extender_1
  Shifter #(.width(32)) shifter_1 (.in(bit_extender_1_out), .\dist (5'b00010), .out(shifter_1_out));
  _4_Controller_main main_4 (
    .Op_code(main_2_instruction_2_4), .Fuct_code(main_2_instruction_2), .RegWrite(main_4_regwrite),
    .RegDst(main_4_regdst), .ALUSrc(main_4_alusrc), .Branch(main_4_branch), .MemWrite(main_4_memwrite),
    .MemToReg(main_4_memtoreg), .JToPC(main_4_jtopc), .Op_3(main_4_op_3), .Op_2_0(main_4_op_2_0),
    .shamt_code(main_2_instruction_2_2));  // open: shamt_zero, Shift_Left
  _1_Register_file_main main_5 (
    .A1(main_2_instruction_2_3[25:21]), .CLK(clock_1_out), .A2(main_2_instruction_2_3[20:16]), .WD(WB_data),
    .A3(main_10_write_add_2), .Write_EN(main_10_regwrite_2), .RD1(main_5_rd1), .RD1_2(main_5_rd1_2));
  assign bit_extender_2_out = {{2{main_2_instruction_2_3[25]}}, {main_2_instruction_2_3, main_2_instruction_2_2, main_2_instruction_2}};  // Bit_Extender bit_extender_2
  Adder #(.width(32)) adder_2 (.a(shifter_1_out), .b(main_2_pc_4_2), .out(adder_2_out));  // open: cin, cout
  // Probe on multiplexer_3_out
  Multiplexer #(.width(32)) multiplexer_3 (
    .in0(main_5_rd1), .in1(MemtoRegM), .out(multiplexer_3_out), .sel(Forward_RsD));  // open: en
  // Probe on multiplexer_4_out
  Multiplexer #(.width(32)) multiplexer_4 (
    .in0(main_5_rd1_2), .in1(WB_data), .out(multiplexer_4_out), .sel(Forward_RtD));  // open: en
  // Probe on main_2_instruction_2_3[25:21]
  // Probe on main_2_instruction_2_3[20:16]
  _5_2_Register_main main_6 (
    .CLK(clock_1_out), .RD1(multiplexer_3_out), .RD2(multiplexer_4_out), .rs(main_2_instruction_2_3[25:21]),
    .rt(main_2_instruction_2_3[20:16]), .imm_0_15(bit_extender_1_out), .imm_0_25(bit_extender_2_out),
    .RD1_3(main_6_rd1_3), .RD2_2(main_6_rd2_2), .rs_21_25(main_6_rs_21_25), .rt_16_20(main_6_rt_16_20),
    .imm_0_15_2(main_6_imm_0_15_2), .imm_0_25_2(main_6_imm_0_25_2), .RD1_2(main_6_rd1_2),
    .RD1_4(main_6_rd1_4), .RD1_5(main_6_rd1_5), .RD1_7(main_6_rd1_7), .RD1_8(main_6_rd1_8),
    .RD1_9(main_6_rd1_9), .RD1_10(main_6_rd1_10), .in_4(main_4_jtopc), .in_6(main_4_memtoreg),
    .in_8(main_4_memwrite), .in_12(main_4_op_2_0), .in_14(main_4_op_3), .in_15(main_4_alusrc),
    .in_19(main_4_regdst), .RegWrite(main_4_regwrite), .RegWrite_2(main_6_regwrite_2),
    .rd(main_2_instruction_2_3[15:11]), .rd_11_15(main_6_rd_11_15), .CLR(main_1_clear_execute));  // open: PC_4, PC_4_2, RD1_6, in_10
  // Probe on main_6_rs_21_25
  // Probe on main_6_rt_16_20
  Multiplexer #(.width(5)) multiplexer_5 (
    .in0(main_6_rt_16_20), .in1(main_6_rd_11_15), .out(multiplexer_5_out), .sel(main_6_rd1_10));  // open: en
  Multiplexer #(.select(2), .width(32)) multiplexer_6 (
    .in0(main_6_rd2_2), .in1(WB_data), .in2(ALU_result), .out(multiplexer_6_out), .sel(main_1_forward_rt));  // open: in3, en
  // Probe on main_1_forward_rt
  Multiplexer #(.width(32)) multiplexer_7 (
    .in0(multiplexer_6_out), .in1(main_6_imm_0_15_2), .out(multiplexer_7_out), .sel(main_6_rd1_9));  // open: en
  // Probe on main_1_forward_rs
  Shifter #(.width(28)) shifter_2 (.in(main_6_imm_0_25_2), .\dist (5'b00010), .out(shifter_2_out));
  // Probe on multiplexer_8_out
  Multiplexer #(.select(2), .width(32)) multiplexer_8 (
    .in0(main_6_rd1_3), .in1(WB_data), .in2(ALU_result), .out(multiplexer_8_out), .sel(main_1_forward_rs));  // open: in3, en
  _2_ALU_main main_7 (
    .SrcA(multiplexer_8_out), .SrcB(multiplexer_7_out), .ALU_result(main_7_alu_result),
    .Op_1_0(main_6_rd1_8), .Op_2_0(main_6_rd1_7));  // open: beq
  // Probe on multiplexer_6_out
  _5_3_Register_main main_8 (
    .CLK(clock_1_out), .ALU_result(main_7_alu_result), .rt_data(multiplexer_6_out),
    .Write_add(multiplexer_5_out), .ALU_result_2(ALU_result), .rt_data_2(main_8_rt_data_2),
    .Write_add_2(main_8_write_add_2), .RD1_2(main_8_rd1_2), .RD1_3(main_8_rd1_3), .RD1_4(main_8_rd1_4),
    .in_2(main_6_rd1_2), .in_4(main_6_rd1_4), .in_6(main_6_rd1_5), .jump_add(shifter_2_out),
    .jump_add_2(main_8_jump_add_2), .in_9(main_6_regwrite_2), .RD1_6(main_8_rd1_6));  // open: RD1, beq_add, beq, beq_add_2, RD1_5, in_7
  // Probe on ALU_result
  // Probe on main_8_rt_data_2
  // Probe on main_8_write_add_2
  // Probe on MemtoRegM
  _3_Data_memory_main main_9 (
    .input_address(ALU_result[23:0]), .Write_EN(main_8_rd1_4), .input_data(main_8_rt_data_2),
    .output_data(MemtoRegM), .CLK(clock_1_out));
  _5_4_Register_main main_10 (
    .CLK(clock_1_out), .ALU_result(ALU_result), .Read_data(MemtoRegM), .Write_add(main_8_write_add_2),
    .ALU_result_2(main_10_alu_result_2), .Read_data_2(main_10_read_data_2),
    .Write_add_2(main_10_write_add_2), .RD1(main_10_rd1), .in_2(main_8_rd1_3), .RegWrite(main_8_rd1_6),
    .RegWrite_2(main_10_regwrite_2));
  Multiplexer #(.width(32)) multiplexer_9 (
    .in0(main_10_alu_result_2), .in1(main_10_read_data_2), .out(WB_data), .sel(main_10_rd1));  // open: en
  // Probe on main_10_write_add_2
  // Probe on WB_data

  // Notes on the sheet:
  //   beq_add
  //   CLK
  //   jump_add
  //   24bits address
  //   contents of rom_1 (hex, n*v repeats v):
  //   0 20100002 20110005 ae110004 0 8e120004 22530004 12320003 0 0 0 8000011 5*0 ffffffff
  //   beq
  //   PC+4
  //   immediate(I-type)
  //   immediate(J-type)
  //   RsD
  //   RtD
  //   RdD
  //   RsE
  //   RtE
  //   RdE
  //   MemtoRegE
  //   RegDst
  //   ALU_OP(3)
  //   ALU_Src
  //   ALU_OP(2:0)
  //   jump
  //   MemWriteM
  //   RegWriteM
  //   WriteRegM
  //   MemtoRegB
  //   RegWriteW
  //   WriteRegW
  //   Write_data
endmodule
