// Logisim project 1_Register_file.circ as structural Verilog: 1 circuit, main circuit main
module main (
  input  [4:0] A1,
  input  CLK,
  input  [4:0] A2,
  input  [31:0] WD,
  input  [4:0] A3,
  input  Write_EN,
  output [31:0] RD1,
  output [31:0] RD1_2
);

  wire demultiplexer_1_out0, demultiplexer_1_out1, demultiplexer_1_out2, demultiplexer_1_out3,
       demultiplexer_1_out4, demultiplexer_1_out5, demultiplexer_1_out6, demultiplexer_1_out7,
       demultiplexer_1_out8, demultiplexer_1_out9, demultiplexer_1_out10, demultiplexer_1_out11,
       demultiplexer_1_out12, demultiplexer_1_out13, demultiplexer_1_out14, demultiplexer_1_out15,
       demultiplexer_1_out16, demultiplexer_1_out17, demultiplexer_1_out18, demultiplexer_1_out19,
       demultiplexer_1_out20, demultiplexer_1_out21, demultiplexer_1_out22, demultiplexer_1_out23,
       demultiplexer_1_out24, demultiplexer_1_out25, demultiplexer_1_out26, demultiplexer_1_out27,
       demultiplexer_1_out28, demultiplexer_1_out29, demultiplexer_1_out30, demultiplexer_1_out31;
  wire [31:0] Address00000_q, Address00001_q, Address00010_q, Address00011_q, Address00100_q, Address00101_q,
       Address00110_q, Address00111_q, Address01000_q, Address01001_q, Address01010_q, Address01011_q,
       Address01100_q, Address01101_q, Address01110_q, Address01111_q, Address10000_q, Address10001_q,
       Address10010_q, Address10011_q, Address10100_q, Address10101_q, Address10110_q, Address10111_q,
       Address11000_q, Address11001_q, Address11010_q, Address11011_q, Address11100_q, Address11101_q,
       Address11110_q, Address11111_q, demultiplexer_2_out0, demultiplexer_2_out1, demultiplexer_2_out2,
       demultiplexer_2_out3, demultiplexer_2_out4, demultiplexer_2_out5, demultiplexer_2_out6,
       demultiplexer_2_out7, demultiplexer_2_out8, demultiplexer_2_out9, demultiplexer_2_out10,
       demultiplexer_2_out11, demultiplexer_2_out12, demultiplexer_2_out13, demultiplexer_2_out14,
       demultiplexer_2_out15, demultiplexer_2_out16, demultiplexer_2_out17, demultiplexer_2_out18,
       demultiplexer_2_out19, demultiplexer_2_out20, demultiplexer_2_out21, demultiplexer_2_out22,
       demultiplexer_2_out23, demultiplexer_2_out24, demultiplexer_2_out25, demultiplexer_2_out26,
       demultiplexer_2_out27, demultiplexer_2_out28, demultiplexer_2_out29, demultiplexer_2_out30,
       demultiplexer_2_out31;

  Demultiplexer #(.select(5)) demultiplexer_1 (
    .out0(demultiplexer_1_out0), .out1(demultiplexer_1_out1), .out2(demultiplexer_1_out2),
    .out3(demultiplexer_1_out3), .out4(demultiplexer_1_out4), .out5(demultiplexer_1_out5),
    .out6(demultiplexer_1_out6), .out7(demultiplexer_1_out7), .out8(demultiplexer_1_out8),
    .out9(demultiplexer_1_out9), .out10(demultiplexer_1_out10), .out11(demultiplexer_1_out11),
    .out12(demultiplexer_1_out12), .out13(demultiplexer_1_out13), .out14(demultiplexer_1_out14),
    .out15(demultiplexer_1_out15), .out16(demultiplexer_1_out16), .out17(demultiplexer_1_out17),
    .out18(demultiplexer_1_out18), .out19(demultiplexer_1_out19), .out20(demultiplexer_1_out20),
    .out21(demultiplexer_1_out21), .out22(demultiplexer_1_out22), .out23(demultiplexer_1_out23),
    .out24(demultiplexer_1_out24), .out25(demultiplexer_1_out25), .out26(demultiplexer_1_out26),
    .out27(demultiplexer_1_out27), .out28(demultiplexer_1_out28), .out29(demultiplexer_1_out29),
    .out30(demultiplexer_1_out30), .out31(demultiplexer_1_out31), .in(Write_EN), .sel(A3));  // open: en
  Demultiplexer #(.select(5), .width(32)) demultiplexer_2 (
    .out0(demultiplexer_2_out0), .out1(demultiplexer_2_out1), .out2(demultiplexer_2_out2),
    .out3(demultiplexer_2_out3), .out4(demultiplexer_2_out4), .out5(demultiplexer_2_out5),
    .out6(demultiplexer_2_out6), .out7(demultiplexer_2_out7), .out8(demultiplexer_2_out8),
    .out9(demultiplexer_2_out9), .out10(demultiplexer_2_out10), .out11(demultiplexer_2_out11),
    .out12(demultiplexer_2_out12), .out13(demultiplexer_2_out13), .out14(demultiplexer_2_out14),
    .out15(demultiplexer_2_out15), .out16(demultiplexer_2_out16), .out17(demultiplexer_2_out17),
    .out18(demultiplexer_2_out18), .out19(demultiplexer_2_out19), .out20(demultiplexer_2_out20),
    .out21(demultiplexer_2_out21), .out22(demultiplexer_2_out22), .out23(demultiplexer_2_out23),
    .out24(demultiplexer_2_out24), .out25(demultiplexer_2_out25), .out26(demultiplexer_2_out26),
    .out27(demultiplexer_2_out27), .out28(demultiplexer_2_out28), .out29(demultiplexer_2_out29),
    .out30(demultiplexer_2_out30), .out31(demultiplexer_2_out31), .in(WD), .sel(A3));  // open: en
  Register #(.width(32)) Address00000 (
    .D(demultiplexer_2_out0), .en(demultiplexer_1_out0), .Q(Address00000_q), .clk(CLK));  // open: clr
  Register #(.width(32)) Address00001 (
    .D(demultiplexer_2_out1), .en(demultiplexer_1_out1), .Q(Address00001_q), .clk(CLK));  // open: clr
  Register #(.width(32)) Address00010 (
    .D(demultiplexer_2_out2), .en(demultiplexer_1_out2), .Q(Address00010_q), .clk(CLK));  // open: clr
  Register #(.width(32)) Address00011 (
    .D(demultiplexer_2_out3), .en(demultiplexer_1_out3), .Q(Address00011_q), .clk(CLK));  // open: clr
  Register #(.width(32)) Address00100 (
    .D(demultiplexer_2_out4), .en(demultiplexer_1_out4), .Q(Address00100_q), .clk(CLK));  // open: clr
  Register #(.width(32)) Address00101 (
    .D(demultiplexer_2_out5), .en(demultiplexer_1_out5), .Q(Address00101_q), .clk(CLK));  // open: clr
  Register #(.width(32)) Address00110 (
    .D(demultiplexer_2_out6), .en(demultiplexer_1_out6), .Q(Address00110_q), .clk(CLK));  // open: clr
  Register #(.width(32)) Address00111 (
    .D(demultiplexer_2_out7), .en(demultiplexer_1_out7), .Q(Address00111_q), .clk(CLK));  // open: clr
  Register #(.width(32)) Address01000 (
    .D(demultiplexer_2_out8), .en(demultiplexer_1_out8), .Q(Address01000_q), .clk(CLK));  // open: clr
  Register #(.width(32)) Address01001 (
    .D(demultiplexer_2_out9), .en(demultiplexer_1_out9), .Q(Address01001_q), .clk(CLK));  // open: clr
  Register #(.width(32)) Address01010 (
    .D(demultiplexer_2_out10), .en(demultiplexer_1_out10), .Q(Address01010_q), .clk(CLK));  // open: clr
  Register #(.width(32)) Address01011 (
    .D(demultiplexer_2_out11), .en(demultiplexer_1_out11), .Q(Address01011_q), .clk(CLK));  // open: clr
  Register #(.width(32)) Address01100 (
    .D(demultiplexer_2_out12), .en(demultiplexer_1_out12), .Q(Address01100_q), .clk(CLK));  // open: clr
  Register #(.width(32)) Address01101 (
    .D(demultiplexer_2_out13), .en(demultiplexer_1_out13), .Q(Address01101_q), .clk(CLK));  // open: clr
  Register #(.width(32)) Address01110 (
    .D(demultiplexer_2_out14), .en(demultiplexer_1_out14), .Q(Address01110_q), .clk(CLK));  // open: clr
  Register #(.width(32)) Address01111 (
    .D(demultiplexer_2_out15), .en(demultiplexer_1_out15), .Q(Address01111_q), .clk(CLK));  // open: clr
  Register #(.width(32)) Address10000 (
    .D(demultiplexer_2_out16), .en(demultiplexer_1_out16), .Q(Address10000_q), .clk(CLK));  // open: clr
  Register #(.width(32)) Address10001 (
    .D(demultiplexer_2_out17), .en(demultiplexer_1_out17), .Q(Address10001_q), .clk(CLK));  // open: clr
  Register #(.width(32)) Address10010 (
    .D(demultiplexer_2_out18), .en(demultiplexer_1_out18), .Q(Address10010_q), .clk(CLK));  // open: clr
  Register #(.width(32)) Address10011 (
    .D(demultiplexer_2_out19), .en(demultiplexer_1_out19), .Q(Address10011_q), .clk(CLK));  // open: clr
  Register #(.width(32)) Address10100 (
    .D(demultiplexer_2_out20), .en(demultiplexer_1_out20), .Q(Address10100_q), .clk(CLK));  // open: clr
  Register #(.width(32)) Address10101 (
    .D(demultiplexer_2_out21), .en(demultiplexer_1_out21), .Q(Address10101_q), .clk(CLK));  // open: clr
  Register #(.width(32)) Address10110 (
    .D(demultiplexer_2_out22), .en(demultiplexer_1_out22), .Q(Address10110_q), .clk(CLK));  // open: clr
  Register #(.width(32)) Address10111 (
    .D(demultiplexer_2_out23), .en(demultiplexer_1_out23), .Q(Address10111_q), .clk(CLK));  // open: clr
  Register #(.width(32)) Address11000 (
    .D(demultiplexer_2_out24), .en(demultiplexer_1_out24), .Q(Address11000_q), .clk(CLK));  // open: clr
  Register #(.width(32)) Address11001 (
    .D(demultiplexer_2_out25), .en(demultiplexer_1_out25), .Q(Address11001_q), .clk(CLK));  // open: clr
  Register #(.width(32)) Address11010 (
    .D(demultiplexer_2_out26), .en(demultiplexer_1_out26), .Q(Address11010_q), .clk(CLK));  // open: clr
  Register #(.width(32)) Address11011 (
    .D(demultiplexer_2_out27), .en(demultiplexer_1_out27), .Q(Address11011_q), .clk(CLK));  // open: clr
  Register #(.width(32)) Address11100 (
    .D(demultiplexer_2_out28), .en(demultiplexer_1_out28), .Q(Address11100_q), .clk(CLK));  // open: clr
  Register #(.width(32)) Address11101 (
    .D(demultiplexer_2_out29), .en(demultiplexer_1_out29), .Q(Address11101_q), .clk(CLK));  // open: clr
  Register #(.width(32)) Address11110 (
    .D(demultiplexer_2_out30), .en(demultiplexer_1_out30), .Q(Address11110_q), .clk(CLK));  // open: clr
  Register #(.width(32)) Address11111 (
    .D(demultiplexer_2_out31), .en(demultiplexer_1_out31), .Q(Address11111_q), .clk(CLK));  // open: clr
  // Probe on Address10000_q
  // Probe on Address10001_q
  // Probe on Address10010_q
  // Probe on Address10011_q
  Multiplexer #(.select(5), .width(32)) multiplexer_1 (
    .in0(Address00000_q), .in1(Address00001_q), .in2(Address00010_q), .in3(Address00011_q),
    .in4(Address00100_q), .in5(Address00101_q), .in6(Address00110_q), .in7(Address00111_q),
    .in8(Address01000_q), .in9(Address01001_q), .in10(Address01010_q), .in11(Address01011_q),
    .in12(Address01100_q), .in13(Address01101_q), .in14(Address01110_q), .in15(Address01111_q),
    .in16(Address10000_q), .in17(Address10001_q), .in18(Address10010_q), .in19(Address10011_q),
    .in20(Address10100_q), .in21(Address10101_q), .in22(Address10110_q), .in23(Address10111_q),
    .in24(Address11000_q), .in25(Address11001_q), .in26(Address11010_q), .in27(Address11011_q),
    .in28(Address11100_q), .in29(Address11101_q), .in30(Address11110_q), .in31(Address11111_q), .out(RD1),
    .sel(A1));  // open: en
  Multiplexer #(.select(5), .width(32)) multiplexer_2 (
    .in0(Address00000_q), .in1(Address00001_q), .in2(Address00010_q), .in3(Address00011_q),
    .in4(Address00100_q), .in5(Address00101_q), .in6(Address00110_q), .in7(Address00111_q),
    .in8(Address01000_q), .in9(Address01001_q), .in10(Address01010_q), .in11(Address01011_q),
    .in12(Address01100_q), .in13(Address01101_q), .in14(Address01110_q), .in15(Address01111_q),
    .in16(Address10000_q), .in17(Address10001_q), .in18(Address10010_q), .in19(Address10011_q),
    .in20(Address10100_q), .in21(Address10101_q), .in22(Address10110_q), .in23(Address10111_q),
    .in24(Address11000_q), .in25(Address11001_q), .in26(Address11010_q), .in27(Address11011_q),
    .in28(Address11100_q), .in29(Address11101_q), .in30(Address11110_q), .in31(Address11111_q), .out(RD1_2),
    .sel(A2));  // open: en
endmodule
