// Logisim project 4_ALU_Control.circ as structural Verilog: 1 circuit, main circuit main
module main (
  input  ALU_Op1,
  input  ALU_Op0,
  input  Funct5,
  input  Funct4,
  input  Funct3,
  input  Funct2,
  input  Funct1,
  input  Funct0,
  output ALU_Control3,
  output ALU_Control2,
  output ALU_Control1,
  output ALU_Control0
);

  wire and_1_out, and_2_out, and_3_out, and_4_out, and_5_out, and_6_out, and_7_out, and_8_out, and_9_out,
       and_10_out, and_11_out, and_12_out, and_13_out, and_14_out, not_1_out, not_2_out, not_3_out,
       not_4_out, not_5_out, not_6_out, not_7_out, not_8_out, not_9_out, not_10_out, not_11_out, not_12_out,
       not_13_out, not_14_out, not_15_out, not_16_out, not_17_out, not_18_out, not_19_out, not_20_out,
       not_21_out;

  not not_1 (not_1_out, ALU_Op1);
  not not_2 (not_2_out, Funct2);
  not not_3 (not_3_out, Funct0);
  not not_4 (not_4_out, Funct2);
  and and_1 (and_1_out, ALU_Op1, not_4_out, Funct0);
  and and_2 (and_2_out, ALU_Op1, Funct1, Funct0);
  and and_3 (and_3_out, ALU_Op1, Funct3, not_5_out);
  not not_5 (not_5_out, Funct1);
  not not_6 (not_6_out, ALU_Op1);
  not not_7 (not_7_out, Funct5);
  not not_8 (not_8_out, Funct2);
  and and_4 (and_4_out, not_7_out, not_8_out, not_9_out);
  not not_9 (not_9_out, Funct0);
  not not_10 (not_10_out, Funct3);
  not not_11 (not_11_out, Funct2);
  and and_5 (and_5_out, not_10_out, not_11_out, not_12_out);
  not not_12 (not_12_out, Funct0);
  not not_13 (not_13_out, Funct2);
  not not_14 (not_14_out, Funct1);
  and and_6 (and_6_out, not_13_out, not_14_out, not_15_out);
  not not_15 (not_15_out, Funct0);
  and and_7 (and_7_out, Funct2, Funct1);
  not not_16 (not_16_out, Funct2);
  and and_8 (and_8_out, Funct4, not_16_out, not_17_out);
  not not_17 (not_17_out, Funct0);
  not not_18 (not_18_out, Funct2);
  not not_19 (not_19_out, Funct1);
  not not_20 (not_20_out, Funct0);
  not not_21 (not_21_out, Funct1);
  and and_9 (and_9_out, not_1_out, ALU_Op0);
  or or_1 (ALU_Control3, and_9_out, and_10_out);
  and and_10 (and_10_out, ALU_Op1, not_2_out, Funct1, not_3_out);
  or or_2 (ALU_Control2, and_1_out, and_2_out, and_3_out);
  and and_11 (and_11_out, ALU_Op1, not_18_out, Funct1, Funct0);
  and and_12 (and_12_out, ALU_Op1, Funct2, not_19_out, Funct0);
  and and_13 (and_13_out, ALU_Op1, Funct2, Funct1, not_20_out);
  and and_14 (and_14_out, ALU_Op1, Funct3, not_21_out);
  or or_3 (ALU_Control1, not_6_out, and_4_out, and_5_out, and_6_out, and_7_out, and_8_out);
  or or_4 (ALU_Control0, and_11_out, and_12_out, and_13_out, and_14_out);
endmodule
