// Logisim project 4_Controller.circ as structural Verilog: 1 circuit, main circuit main
module main (
  input  [5:0] Op_code,
  input  [5:0] Fuct_code,
  input  [4:0] shamt_code,
  output RegWrite,
  output RegDst,
  output ALUSrc,
  output Branch,
  output MemWrite,
  output MemToReg,
  output JToPC,
  output Op_3,
  output [2:0] Op_2_0,
  output Shift_Left,
  output shamt_zero
);

  wire main_1_alu_op0, main_1_alu_op1;

  _4_main_decoder_main main_1 (
    .Op5(Op_code[5]), .Op4(Op_code[4]), .Op3(Op_code[3]), .Op2(Op_code[2]), .Op1(Op_code[1]),
    .Op0(Op_code[0]), .RegWrite(RegWrite), .RegDst(RegDst), .ALUSrc(ALUSrc), .Branch(Branch),
    .MemWrite(MemWrite), .MemToReg(MemToReg), .ALU_Op1(main_1_alu_op1), .ALU_Op0(main_1_alu_op0),
    .JTOPC(JToPC));
  Comparator #(.width(5)) comparator_1 (.a(shamt_code), .b({5{1'b0}}), .eq(shamt_zero));  // open: gt, lt
  _4_ALU_Control_main main_2 (
    .ALU_Op1(main_1_alu_op1), .ALU_Op0(main_1_alu_op0), .Funct5(Fuct_code[5]), .Funct4(Fuct_code[4]),
    .Funct3(Fuct_code[3]), .Funct2(Fuct_code[2]), .Funct1(Fuct_code[1]), .Funct0(Fuct_code[0]),
    .ALU_Control3(Op_3), .ALU_Control2(Op_2_0[2]), .ALU_Control1(Op_2_0[1]), .ALU_Control0(Op_2_0[0]));
  Comparator #(.width(6)) comparator_2 (.a(Fuct_code), .b({6{1'b0}}), .eq(Shift_Left));  // open: gt, lt
endmodule
