// Logisim project 5-1_Register.circ as structural Verilog: 1 circuit, main circuit main
module main (
  input  CLK,
  input  EN,
  input  [31:0] Instruction,
  input  [31:0] PC_4,
  output [31:0] Instruction_2,
  output [31:0] PC_4_2
);

  Register #(.width(32)) u_Instruction (.D(Instruction), .en(EN), .Q(Instruction_2), .clk(CLK));  // open: clr
  Register #(.width(32)) u_PC_4 (.D(PC_4), .en(EN), .Q(PC_4_2), .clk(CLK));  // open: clr
endmodule
