// Logisim project 5-2_Register.circ as structural Verilog: 1 circuit, main circuit main
module main (
  input  [4:0] rd,
  input  CLR,
  input  CLK,
  input  in_4,
  input  [31:0] RD1,
  input  in_6,
  input  [31:0] RD2,
  input  in_8,
  input  [4:0] rs,
  input  in_10,
  input  [4:0] rt,
  input  [2:0] in_12,
  input  [31:0] imm_0_15,
  input  in_14,
  input  in_15,
  input  [31:0] PC_4,
  input  RegWrite,
  input  [27:0] imm_0_25,
  input  in_19,
  output [4:0] rd_11_15,
  output RD1_2,
  output [31:0] RD1_3,
  output RD1_4,
  output [31:0] RD2_2,
  output RD1_5,
  output [4:0] rs_21_25,
  output RD1_6,
  output [4:0] rt_16_20,
  output [2:0] RD1_7,
  output [31:0] imm_0_15_2,
  output RD1_8,
  output RD1_9,
  output [31:0] PC_4_2,
  output RegWrite_2,
  output [27:0] imm_0_25_2,
  output RD1_10
);

  Register #(.width(1)) Jump (.D(in_4), .en(1'b1), .Q(RD1_2), .clk(CLK), .clr(CLR));
  Register #(.width(1)) MemtoReg (.D(in_6), .en(1'b1), .Q(RD1_4), .clk(CLK), .clr(CLR));
  Register #(.width(1)) MemWrite (.D(in_8), .en(1'b1), .Q(RD1_5), .clk(CLK), .clr(CLR));
  Register #(.width(1)) Branch (.D(in_10), .en(1'b1), .Q(RD1_6), .clk(CLK), .clr(CLR));
  Register #(.width(3)) ALU_OP_0_2 (.D(in_12), .en(1'b1), .Q(RD1_7), .clk(CLK), .clr(CLR));
  Register #(.width(1)) ALU_OP_3 (.D(in_14), .en(1'b1), .Q(RD1_8), .clk(CLK), .clr(CLR));
  Register #(.width(1)) ALU_Src (.D(in_15), .en(1'b1), .Q(RD1_9), .clk(CLK), .clr(CLR));
  Register #(.width(1)) u_RegWrite (.D(RegWrite), .en(1'b1), .Q(RegWrite_2), .clk(CLK), .clr(CLR));
  Register #(.width(1)) RegDst (.D(in_19), .en(1'b1), .Q(RD1_10), .clk(CLK), .clr(CLR));
  Register #(.width(5)) u_rd_11_15 (.D(rd), .en(1'b1), .Q(rd_11_15), .clk(CLK), .clr(CLR));
  Register #(.width(32)) u_RD1 (.D(RD1), .en(1'b1), .Q(RD1_3), .clk(CLK), .clr(CLR));
  Register #(.width(32)) u_RD2 (.D(RD2), .en(1'b1), .Q(RD2_2), .clk(CLK), .clr(CLR));
  Register #(.width(5)) rs_16_20 (.D(rs), .en(1'b1), .Q(rs_21_25), .clk(CLK), .clr(CLR));
  Register #(.width(5)) rd_11_15_2 (.D(rt), .en(1'b1), .Q(rt_16_20), .clk(CLK), .clr(CLR));
  Register #(.width(32)) u_imm_0_15 (.D(imm_0_15), .en(1'b1), .Q(imm_0_15_2), .clk(CLK), .clr(CLR));
  Register #(.width(32)) u_PC_4 (.D(PC_4), .en(1'b1), .Q(PC_4_2), .clk(CLK), .clr(CLR));
  Register #(.width(28)) u_imm_0_25 (.D(imm_0_25), .en(1'b1), .Q(imm_0_25_2), .clk(CLK), .clr(CLR));
endmodule
