// Logisim project 5-3_Register.circ as structural Verilog: 1 circuit, main circuit main
module main (
  input  CLK,
  input  in_2,
  input  RD1,
  input  in_4,
  input  [31:0] ALU_result,
  input  in_6,
  input  in_7,
  input  [31:0] rt_data,
  input  in_9,
  input  [4:0] Write_add,
  input  [31:0] beq_add,
  input  [27:0] jump_add,
  output RD1_2,
  output beq,
  output RD1_3,
  output [31:0] ALU_result_2,
  output RD1_4,
  output RD1_5,
  output [31:0] rt_data_2,
  output RD1_6,
  output [4:0] Write_add_2,
  output [31:0] beq_add_2,
  output [27:0] jump_add_2
);

  Register #(.width(1)) Jump (.D(in_2), .Q(RD1_2), .clk(CLK));  // open: en, clr
  Register #(.width(1)) MemtoReg (.D(in_4), .Q(RD1_3), .clk(CLK));  // open: en, clr
  Register #(.width(1)) MemWrite (.D(in_6), .Q(RD1_4), .clk(CLK));  // open: en, clr
  Register #(.width(1)) Branch (.D(in_7), .Q(RD1_5), .clk(CLK));  // open: en, clr
  Register #(.width(1)) RegWrite (.D(in_9), .Q(RD1_6), .clk(CLK));  // open: en, clr
  Register #(.width(1)) u_beq (.D(RD1), .Q(beq), .clk(CLK));  // open: en, clr
  Register #(.width(32)) u_ALU_result (.D(ALU_result), .Q(ALU_result_2), .clk(CLK));  // open: en, clr
  Register #(.width(32)) u_rt_data (.D(rt_data), .Q(rt_data_2), .clk(CLK));  // open: en, clr
  Register #(.width(5)) u_Write_add (.D(Write_add), .Q(Write_add_2), .clk(CLK));  // open: en, clr
  Register #(.width(32)) u_beq_add (.D(beq_add), .Q(beq_add_2), .clk(CLK));  // open: en, clr
  Register #(.width(28)) u_jump_add (.D(jump_add), .Q(jump_add_2), .clk(CLK));  // open: en, clr
endmodule
