// Logisim project 5-4_Register.circ as structural Verilog: 1 circuit, main circuit main
module main (
  input  CLK,
  input  in_2,
  input  [31:0] ALU_result,
  input  RegWrite,
  input  [31:0] Read_data,
  input  [4:0] Write_add,
  output RD1,
  output [31:0] ALU_result_2,
  output RegWrite_2,
  output [31:0] Read_data_2,
  output [4:0] Write_add_2
);

  Register #(.width(1)) MemtoReg (.D(in_2), .Q(RD1), .clk(CLK));  // open: en, clr
  Register #(.width(1)) u_RegWrite (.D(RegWrite), .Q(RegWrite_2), .clk(CLK));  // open: en, clr
  Register #(.width(32)) u_ALU_result (.D(ALU_result), .Q(ALU_result_2), .clk(CLK));  // open: en, clr
  Register #(.width(32)) u_Read_data (.D(Read_data), .Q(Read_data_2), .clk(CLK));  // open: en, clr
  Register #(.width(5)) u_Write_add (.D(Write_add), .Q(Write_add_2), .clk(CLK));  // open: en, clr
endmodule
