// Logisim project Early_Branch.circ as structural Verilog: 1 circuit, main circuit main
module main (
  input  [31:0] in_1,
  input  in_2,
  input  [31:0] in_3,
  output out_4
);

  wire comparator_1_eq;

  Comparator #(.width(32)) comparator_1 (.a(in_1), .b(in_3), .eq(comparator_1_eq));  // open: gt, lt
  and and_1 (out_4, comparator_1_eq, in_2);
endmodule
