// Logisim project Hazard_Stalling&DataForwarding.circ as structural Verilog: 1 circuit, main circuit main
module main (
  input  [4:0] rs_Decode,
  input  CLK,
  input  [4:0] rt_Execute,
  input  [4:0] rt_Decode,
  input  MemtoReg_Execute,
  input  MemtoRegM,
  input  RegWrite_Memory,
  input  [4:0] WriteReg_Memory,
  input  [4:0] rs_Execute,
  input  [4:0] WriteReg_WriteBack,
  input  RegWrite_WriteBack,
  output Clear_Execute,
  output Stall_Fetch_Decode,
  output Forward_RsD,
  output [1:0] Forward_rs,
  output [1:0] Forward_rt,
  output Forward_RtD
);

  wire and_3_out, comparator_1_eq, comparator_2_lt, comparator_3_eq, comparator_4_eq, comparator_5_eq,
       comparator_6_eq, comparator_7_lt, comparator_8_eq, comparator_9_eq, comparator_10_lt,
       comparator_11_eq, comparator_12_lt, d_ff_1_q, or_1_out;

  Comparator #(.width(5)) comparator_1 (.a(WriteReg_Memory), .b(rs_Execute), .eq(comparator_1_eq));  // open: gt, lt
  Comparator #(.width(5)) comparator_2 (.a(rs_Execute), .b({5{1'b0}}), .lt(comparator_2_lt));  // open: gt, eq
  Comparator #(.width(5)) comparator_3 (.a(rs_Execute), .b(WriteReg_WriteBack), .eq(comparator_3_eq));  // open: gt, lt
  Comparator #(.width(5)) comparator_4 (.a(rs_Decode), .b(rt_Execute), .eq(comparator_4_eq));  // open: gt, lt
  Comparator #(.width(5)) comparator_5 (.a(rt_Execute), .b(rt_Decode), .eq(comparator_5_eq));  // open: gt, lt
  and and_1 (Forward_rs[1], RegWrite_Memory, comparator_1_eq, comparator_2_lt);
  and and_2 (Forward_rs[0], comparator_3_eq, comparator_2_lt, RegWrite_WriteBack);
  or or_1 (or_1_out, comparator_4_eq, comparator_5_eq);
  and and_3 (and_3_out, or_1_out, MemtoReg_Execute);
  not not_1 (Stall_Fetch_Decode, and_3_out);
  D_Flip_Flop #(.trigger("falling")) d_ff_1 (.clk(CLK), .D(and_3_out), .Q(d_ff_1_q));  // open: Qn, preset, en, reset
  Comparator #(.width(5)) comparator_6 (.a(WriteReg_Memory), .b(rt_Execute), .eq(comparator_6_eq));  // open: gt, lt
  Comparator #(.width(5)) comparator_7 (.a(rt_Execute), .b({5{1'b0}}), .lt(comparator_7_lt));  // open: gt, eq
  Comparator #(.width(5)) comparator_8 (.a(rt_Execute), .b(WriteReg_WriteBack), .eq(comparator_8_eq));  // open: gt, lt
  and and_4 (Clear_Execute, CLK, d_ff_1_q);
  and and_5 (Forward_rt[1], RegWrite_Memory, comparator_6_eq, comparator_7_lt);
  and and_6 (Forward_rt[0], comparator_8_eq, comparator_7_lt, RegWrite_WriteBack);
  Comparator #(.width(5)) comparator_9 (.a(rs_Decode), .b(WriteReg_Memory), .eq(comparator_9_eq));  // open: gt, lt
  Comparator #(.width(5)) comparator_10 (.a(rs_Decode), .b({5{1'b0}}), .lt(comparator_10_lt));  // open: gt, eq
  Comparator #(.width(5)) comparator_11 (.a(rt_Decode), .b(WriteReg_WriteBack), .eq(comparator_11_eq));  // open: gt, lt
  Comparator #(.width(5)) comparator_12 (.a(rt_Decode), .b({5{1'b0}}), .lt(comparator_12_lt));  // open: gt, eq
  and and_7 (Forward_RsD, MemtoRegM, comparator_9_eq, comparator_10_lt);
  and and_8 (Forward_RtD, comparator_11_eq, comparator_12_lt, RegWrite_WriteBack);
endmodule
