// Logisim project 4_main_decoder.circ as structural Verilog: 1 circuit, main circuit main
module main (
  input  Op5,
  input  Op4,
  input  Op3,
  input  Op2,
  input  Op1,
  input  Op0,
  output RegWrite,
  output RegDst,
  output ALUSrc,
  output Branch,
  output MemWrite,
  output MemToReg,
  output ALU_Op1,
  output ALU_Op0,
  output JTOPC
);

  wire and_2_out, and_3_out, not_1_out, not_2_out, not_3_out, not_4_out, not_5_out, not_6_out, not_7_out,
       not_8_out, not_9_out;

  not not_1 (not_1_out, Op2);
  not not_2 (not_2_out, Op1);
  not not_3 (not_3_out, Op3);
  not not_4 (not_4_out, Op3);
  not not_5 (not_5_out, Op1);
  or or_1 (ALUSrc, Op1, Op3);
  and and_1 (MemWrite, Op5, Op3);
  not not_6 (not_6_out, Op3);
  not not_7 (not_7_out, Op2);
  not not_8 (not_8_out, Op1);
  not not_9 (not_9_out, Op0);
  and and_2 (and_2_out, not_1_out, not_2_out);
  and and_3 (and_3_out, Op5, not_3_out);
  and and_4 (RegDst, not_4_out, not_5_out);
  and and_5 (ALU_Op1, not_6_out, not_7_out, not_8_out);
  and and_6 (JTOPC, Op1, not_9_out);
  or or_2 (RegWrite, and_2_out, and_3_out);

  assign ALU_Op0 = Op2;
  assign Branch = Op2;
  assign MemToReg = Op1;
endmodule
