// Logisim project 0_Main Circuit.circ as structural Verilog: 1 circuit, main circuit main
module main (
);

  wire and_1_out, button_1_out, clock_1_out, main_1_alusrc, main_1_branch, main_1_jtopc, main_1_memtoreg,
       main_1_memwrite, main_1_op_3, main_1_regdst, main_1_regwrite, main_1_shamt_zero, main_4_beq;
  wire [1:0] main_1_out_13;
  wire [2:0] main_1_op_2_0;
  wire [4:0] multiplexer_3_out, rom_1_data_2;
  wire [5:0] rom_1_data, rom_1_data_4;
  wire [7:0] main_4_alu_result_2;
  wire [23:0] main_4_alu_result;
  wire [25:11] rom_1_data_3;
  wire [27:0] adder_1_out, bit_extender_1_out;
  wire [31:0] adder_2_out, bit_extender_2_out, main_2_rd1, main_2_rd1_2, main_3_out_4, main_5_output_data,
       multiplexer_1_out, multiplexer_2_out, multiplexer_4_out, multiplexer_5_out, multiplexer_6_out,
       register_1_q, shifter_1_out, shifter_2_out;

  Clock clock_1 (.out(clock_1_out));
  // Probe on adder_2_out
  Multiplexer #(.width(32)) multiplexer_1 (
    .in0({shifter_1_out[31:28], adder_1_out}), .in1(adder_2_out), .out(multiplexer_1_out), .sel(and_1_out));  // open: en
  // Probe on shifter_1_out
  LED led_1 (.in(clock_1_out));
  Multiplexer #(.width(32)) multiplexer_2 (
    .in0(multiplexer_1_out), .in1(shifter_1_out), .out(multiplexer_2_out), .sel(main_1_jtopc));  // open: en
  Register #(.width(32)) register_1 (
    .D(multiplexer_2_out), .Q(register_1_q), .clk(clock_1_out), .clr(button_1_out));  // open: en
  Button button_1 (.out(button_1_out));
  Adder #(.width(32)) adder_1 (
    .a(register_1_q), .b(32'h4), .out({shifter_1_out[31:28], adder_1_out}));  // open: cin, cout
  // Probe on {shifter_1_out[31:28], adder_1_out}
  ROM #(.addrWidth(24), .dataWidth(32)) rom_1 (
    .addr(register_1_q[25:2]), .data({rom_1_data_4, rom_1_data_3, rom_1_data_2, rom_1_data}));  // open: sel
  // Probe on rom_1_data_3[25:21]
  // Probe on rom_1_data_3[20:16]
  // Probe on rom_1_data_3[15:11]
  assign bit_extender_1_out = {{2{rom_1_data_3[25]}}, {rom_1_data_3, rom_1_data_2, rom_1_data}};  // Bit_Extender bit_extender_1
  // Probe on multiplexer_3_out
  Multiplexer #(.width(5)) multiplexer_3 (
    .in0(rom_1_data_3[20:16]), .in1(rom_1_data_3[15:11]), .out(multiplexer_3_out), .sel(main_1_regdst));  // open: en
  // Probe on multiplexer_4_out
  // Probe on multiplexer_4_out
  // Probe on {rom_1_data_3[15:11], rom_1_data_2, rom_1_data}
  Shifter #(.width(28)) shifter_1 (.in(bit_extender_1_out), .\dist (5'b00010), .out(shifter_1_out[27:0]));
  _4_Controller_main main_1 (
    .Op_code(rom_1_data_4), .Fuct_code(rom_1_data), .RegWrite(main_1_regwrite), .RegDst(main_1_regdst),
    .ALUSrc(main_1_alusrc), .Branch(main_1_branch), .MemWrite(main_1_memwrite), .MemToReg(main_1_memtoreg),
    .JToPC(main_1_jtopc), .Op_3(main_1_op_3), .Op_2_0(main_1_op_2_0), .shamt_code(rom_1_data_2),
    .shamt_zero(main_1_shamt_zero), .out_13(main_1_out_13));
  // Probe on multiplexer_4_out[31:27]
  assign bit_extender_2_out = {{16{rom_1_data_3[15]}}, {rom_1_data_3[15:11], rom_1_data_2, rom_1_data}};  // Bit_Extender bit_extender_2
  // Probe on rom_1_data_2
  // Probe on main_2_rd1_2
  _1_Register_file_main main_2 (
    .A1(rom_1_data_3[25:21]), .CLK(clock_1_out), .A2(rom_1_data_3[20:16]), .WD(multiplexer_4_out),
    .A3(multiplexer_3_out), .Write_EN(main_1_regwrite), .RD1(main_2_rd1), .RD1_2(main_2_rd1_2));
  // Probe on multiplexer_4_out[26:0]
  // Probe on bit_extender_2_out
  // Probe on main_2_rd1_2
  Multiplexer #(.width(32)) multiplexer_4 (
    .in0(main_3_out_4), .in1(multiplexer_6_out), .out(multiplexer_4_out), .sel(main_1_shamt_zero));  // open: en
  _2_ALU2_main main_3 (.in_1(main_2_rd1_2), .in_2(rom_1_data_2), .in_3(main_1_out_13), .out_4(main_3_out_4));
  // Probe on main_2_rd1
  // Probe on main_2_rd1_2
  // Probe on main_3_out_4
  // Probe on main_2_rd1
  // Probe on main_2_rd1_2
  Multiplexer #(.width(32)) multiplexer_5 (
    .in0(main_2_rd1_2), .in1(bit_extender_2_out), .out(multiplexer_5_out), .sel(main_1_alusrc));  // open: en
  Shifter #(.width(32)) shifter_2 (.in(bit_extender_2_out), .\dist (5'b00010), .out(shifter_2_out));
  _2_ALU1_main main_4 (
    .SrcA(main_2_rd1), .SrcB(multiplexer_5_out), .ALU_result({main_4_alu_result_2, main_4_alu_result}),
    .Op_1_0(main_1_op_3), .beq(main_4_beq), .Op_2_0(main_1_op_2_0));
  Adder #(.width(32)) adder_2 (
    .a({shifter_1_out[31:28], adder_1_out}), .b(shifter_2_out), .out(adder_2_out));  // open: cin, cout
  and and_1 (and_1_out, main_1_branch, main_4_beq);
  // Probe on {main_4_alu_result_2, main_4_alu_result}
  _3_Data_memory_main main_5 (
    .input_address(main_4_alu_result), .Write_EN(main_1_memwrite), .input_data(main_2_rd1_2),
    .output_data(main_5_output_data), .CLK(clock_1_out));
  // Probe on multiplexer_6_out
  Multiplexer #(.width(32)) multiplexer_6 (
    .in0({main_4_alu_result_2, main_4_alu_result}), .in1(main_5_output_data), .out(multiplexer_6_out),
    .sel(main_1_memtoreg));  // open: en
  // Probe on multiplexer_6_out

  // Notes on the sheet:
  //   CLK
  //   24bits address
  //   contents of rom_1 (hex, n*v repeats v):
  //   0 20100002 20110005 ae110004 8e120004 12320003 0 0 0 800000c 0 0 2749824 2749823 2749825 2749827
  //   2749826 2749828 2119821 274a020 274a822 2959020 232a82a 15a900 15a901 108942 114083 124883
  //   rd
  //   immediate
endmodule
