// Logisim project 2_ALU1.circ as structural Verilog: 1 circuit, main circuit main
module main (
  input  [31:0] SrcA,
  input  [31:0] SrcB,
  input  Op_1_0,
  input  [2:0] Op_2_0,
  output beq,
  output [31:0] ALU_result
);

  wire bitselector_1_out;
  wire [31:0] adder_1_out, AND_out, bit_extender_1_out, multiplexer_1_out, multiplexer_2_out,
       multiplier_1_out, NAND_out, NOR_out, not_1_out, OR_out, XNOR_out, XOR_out;

  assign not_1_out = ~SrcB;  // NOT_Gate not_1, 32 bits wide
  Multiplexer #(.width(32)) multiplexer_1 (
    .in0(SrcB), .in1(not_1_out), .out(multiplexer_1_out), .sel(Op_1_0));  // open: en
  Adder #(.width(32)) adder_1 (.a(multiplexer_1_out), .b(SrcA), .out(adder_1_out), .cin(Op_1_0), .cout(beq));
  Multiplier #(.width(32)) multiplier_1 (.a(multiplexer_1_out), .b(SrcA), .out(multiplier_1_out));  // open: cin, cout
  BitSelector #(.width(32)) bitselector_1 (.in(adder_1_out), .out(bitselector_1_out), .sel({5{1'b1}}));
  assign AND_out = SrcA & SrcB;  // AND_Gate AND, 32 bits wide
  assign bit_extender_1_out = {{31{bitselector_1_out}}, bitselector_1_out};  // Bit_Extender bit_extender_1
  Multiplexer #(.width(32)) multiplexer_2 (
    .in0(AND_out), .in1(bit_extender_1_out), .out(multiplexer_2_out), .sel(Op_1_0));  // open: en
  assign OR_out = SrcA | SrcB;  // OR_Gate OR, 32 bits wide
  Multiplexer #(.select(3), .width(32)) multiplexer_3 (
    .in0(multiplexer_2_out), .in1(OR_out), .in2(adder_1_out), .in3(XOR_out), .in4(multiplier_1_out),
    .in5(NAND_out), .in6(NOR_out), .in7(XNOR_out), .out(ALU_result), .sel(Op_2_0));  // open: en
  assign NAND_out = ~(SrcA & SrcB);  // NAND_Gate NAND, 32 bits wide
  assign NOR_out = ~(SrcA | SrcB);  // NOR_Gate NOR, 32 bits wide
  assign XOR_out = SrcA ^ SrcB;  // XOR_Gate XOR, 32 bits wide
  assign XNOR_out = ~(SrcA ^ SrcB);  // XNOR_Gate XNOR, 32 bits wide
endmodule
