// Logisim project 2_ALU2.circ as structural Verilog: 1 circuit, main circuit main
module main (
  input  [31:0] in_1,
  input  [4:0] in_2,
  input  [1:0] in_3,
  output [31:0] out_4
);

  wire comparator_1_lt, comparator_33_gt, comparator_34_gt, comparator_35_gt, comparator_36_gt,
       comparator_37_gt, comparator_38_gt, comparator_39_gt, comparator_40_gt, comparator_41_gt,
       comparator_42_gt, comparator_43_gt, comparator_44_gt;
  wire [4:0] adder_13_out, bitadder_1_out;
  wire [30:0] comparator_2_lt, not_1_out;
  wire [31:0] adder_1_out, adder_2_out, adder_3_out, adder_4_out, adder_5_out, adder_6_out, adder_7_out,
       adder_8_out, adder_9_out, adder_10_out, adder_11_out, bit_extender_1_out, bit_extender_2_out,
       divider_1_out, divider_2_out, divider_3_out, divider_4_out, divider_5_out, divider_6_out,
       divider_7_out, divider_8_out, divider_9_out, divider_10_out, divider_11_out, divider_12_out,
       divider_13_out, divider_14_out, divider_15_out, divider_16_out, divider_17_out, divider_18_out,
       divider_19_out, divider_20_out, divider_21_out, divider_22_out, divider_23_out, divider_24_out,
       divider_25_out, divider_26_out, divider_27_out, divider_28_out, divider_29_out, divider_30_out,
       divider_31_out, divider_32_out, divider_33_out, divider_34_out, divider_35_out, divider_36_out,
       divider_37_out, divider_38_out, divider_39_out, divider_40_out, divider_41_out, divider_42_out,
       divider_43_out, divider_44_out, divider_45_out, divider_46_out, divider_47_out, divider_48_out,
       divider_49_out, divider_50_out, divider_51_out, divider_52_out, divider_53_out, divider_54_out,
       divider_55_out, divider_56_out, divider_57_out, divider_58_out, divider_59_out, divider_60_out,
       divider_61_out, divider_62_out, divider_63_out, divider_64_out, divider_65_out, divider_66_out, F1,
       F2, F3, F4, F5, F6, F7, F8, F9, F10, F11, F12, log, multiplexer_4_out, multiplexer_8_out,
       multiplexer_9_out, multiplexer_10_out, multiplexer_14_out, multiplexer_15_out, multiplexer_16_out,
       multiplexer_20_out, multiplexer_21_out, multiplexer_22_out, multiplexer_26_out, multiplexer_27_out,
       multiplier_1_out, multiplier_2_out, multiplier_3_out, multiplier_4_out, multiplier_5_out,
       multiplier_6_out, multiplier_7_out, multiplier_8_out, multiplier_9_out, multiplier_10_out,
       multiplier_11_out, multiplier_12_out, multiplier_13_out, multiplier_14_out, multiplier_15_out,
       multiplier_16_out, multiplier_17_out, multiplier_18_out, multiplier_19_out, multiplier_20_out,
       multiplier_21_out, multiplier_22_out, multiplier_23_out, multiplier_24_out, multiplier_25_out,
       multiplier_26_out, multiplier_27_out, multiplier_28_out, multiplier_29_out, multiplier_30_out,
       multiplier_31_out, multiplier_33_out, multiplier_34_out, multiplier_35_out, multiplier_36_out,
       multiplier_37_out, multiplier_38_out, multiplier_39_out, multiplier_40_out, multiplier_41_out,
       multiplier_42_out, multiplier_43_out, multiplier_44_out, rt_data, shifter_1_out, shifter_2_out,
       shifter_3_out, square, under;

  Multiplexer #(.width(32)) multiplexer_1 (.in1(in_1), .out(rt_data), .sel(comparator_1_lt));  // open: in0, en
  Comparator #(.width(5)) comparator_1 (.a({5{1'b0}}), .b(in_2), .lt(comparator_1_lt));  // open: gt, eq
  Multiplier #(.width(32)) multiplier_1 (.a(multiplier_2_out), .b(rt_data), .out(multiplier_1_out));  // open: cin, cout
  Multiplier #(.width(32)) multiplier_2 (.a(rt_data), .b(rt_data), .out(multiplier_2_out));  // open: cin, cout
  Multiplier #(.width(32)) multiplier_3 (
    .a(multiplier_25_out), .b(rt_data), .out(multiplier_3_out));  // open: cin, cout
  Multiplier #(.width(32)) multiplier_4 (
    .a(multiplier_26_out), .b(rt_data), .out(multiplier_4_out));  // open: cin, cout
  Multiplier #(.width(32)) multiplier_5 (
    .a(multiplier_27_out), .b(rt_data), .out(multiplier_5_out));  // open: cin, cout
  Multiplier #(.width(32)) multiplier_6 (.a(multiplier_1_out), .b(rt_data), .out(multiplier_6_out));  // open: cin, cout
  Multiplier #(.width(32)) multiplier_7 (.a(multiplier_8_out), .b(rt_data), .out(multiplier_7_out));  // open: cin, cout
  Multiplier #(.width(32)) multiplier_8 (.a(multiplier_3_out), .b(rt_data), .out(multiplier_8_out));  // open: cin, cout
  Multiplier #(.width(32)) multiplier_9 (
    .a(multiplier_10_out), .b(rt_data), .out(multiplier_9_out));  // open: cin, cout
  Multiplier #(.width(32)) multiplier_10 (
    .a(multiplier_4_out), .b(rt_data), .out(multiplier_10_out));  // open: cin, cout
  Multiplier #(.width(32)) multiplier_11 (
    .a(multiplier_12_out), .b(rt_data), .out(multiplier_11_out));  // open: cin, cout
  Multiplier #(.width(32)) multiplier_12 (
    .a(multiplier_5_out), .b(rt_data), .out(multiplier_12_out));  // open: cin, cout
  Multiplier #(.width(32)) multiplier_13 (
    .a(multiplier_14_out), .b(rt_data), .out(multiplier_13_out));  // open: cin, cout
  Multiplier #(.width(32)) multiplier_14 (
    .a(multiplier_6_out), .b(rt_data), .out(multiplier_14_out));  // open: cin, cout
  Multiplier #(.width(32)) multiplier_15 (
    .a(multiplier_7_out), .b(rt_data), .out(multiplier_15_out));  // open: cin, cout
  Multiplier #(.width(32)) multiplier_16 (
    .a(multiplier_9_out), .b(rt_data), .out(multiplier_16_out));  // open: cin, cout
  Multiplier #(.width(32)) multiplier_17 (
    .a(multiplier_11_out), .b(rt_data), .out(multiplier_17_out));  // open: cin, cout
  Multiplier #(.width(32)) multiplier_18 (
    .a(multiplier_13_out), .b(rt_data), .out(multiplier_18_out));  // open: cin, cout
  Multiplier #(.width(32)) multiplier_19 (
    .a(multiplier_20_out), .b(rt_data), .out(multiplier_19_out));  // open: cin, cout
  Multiplier #(.width(32)) multiplier_20 (
    .a(multiplier_15_out), .b(rt_data), .out(multiplier_20_out));  // open: cin, cout
  Multiplier #(.width(32)) multiplier_21 (
    .a(multiplier_16_out), .b(rt_data), .out(multiplier_21_out));  // open: cin, cout
  Multiplier #(.width(32)) multiplier_22 (
    .a(multiplier_21_out), .b(rt_data), .out(multiplier_22_out));  // open: cin, cout
  Multiplier #(.width(32)) multiplier_23 (
    .a(multiplier_17_out), .b(rt_data), .out(multiplier_23_out));  // open: cin, cout
  Multiplier #(.width(32)) multiplier_24 (
    .a(multiplier_23_out), .b(rt_data), .out(multiplier_24_out));  // open: cin, cout
  Multiplier #(.width(32)) multiplier_25 (
    .a(multiplier_18_out), .b(rt_data), .out(multiplier_25_out));  // open: cin, cout
  Multiplier #(.width(32)) multiplier_26 (
    .a(multiplier_19_out), .b(rt_data), .out(multiplier_26_out));  // open: cin, cout
  Multiplier #(.width(32)) multiplier_27 (
    .a(multiplier_22_out), .b(rt_data), .out(multiplier_27_out));  // open: cin, cout
  Multiplier #(.width(32)) multiplier_28 (
    .a(multiplier_29_out), .b(rt_data), .out(multiplier_28_out));  // open: cin, cout
  Multiplier #(.width(32)) multiplier_29 (
    .a(multiplier_24_out), .b(rt_data), .out(multiplier_29_out));  // open: cin, cout
  Multiplier #(.width(32)) multiplier_30 (
    .a(multiplier_28_out), .b(rt_data), .out(multiplier_30_out));  // open: cin, cout
  Shifter #(.width(32), .shift("lr")) shifter_1 (.in(rt_data), .\dist (in_2), .out(shifter_1_out));
  Shifter #(.width(32)) shifter_2 (.in(rt_data), .\dist (in_2), .out(shifter_2_out));
  Multiplexer #(.select(5), .width(32)) multiplexer_2 (
    .in0(32'h1), .in1(rt_data), .in2(multiplier_2_out), .in3(multiplier_1_out), .in4(multiplier_6_out),
    .in5(multiplier_14_out), .in6(multiplier_13_out), .in7(multiplier_18_out), .in8(multiplier_25_out),
    .in9(multiplier_3_out), .in10(multiplier_8_out), .in11(multiplier_7_out), .in12(multiplier_15_out),
    .in13(multiplier_20_out), .in14(multiplier_19_out), .in15(multiplier_26_out), .in16(multiplier_4_out),
    .in17(multiplier_10_out), .in18(multiplier_9_out), .in19(multiplier_16_out), .in20(multiplier_21_out),
    .in21(multiplier_22_out), .in22(multiplier_27_out), .in23(multiplier_5_out), .in24(multiplier_12_out),
    .in25(multiplier_11_out), .in26(multiplier_17_out), .in27(multiplier_23_out), .in28(multiplier_24_out),
    .in29(multiplier_29_out), .in30(multiplier_28_out), .in31(multiplier_30_out), .out(square), .sel(in_2));  // open: en
  Multiplexer #(.select(2), .width(32)) multiplexer_3 (
    .in0(shifter_2_out), .in1(shifter_1_out), .in2(square), .in3(log), .out(out_4), .sel(in_3));  // open: en
  Adder #(.width(32)) adder_1 (.a(F1), .b(F2), .out(adder_1_out));  // open: cin, cout
  Adder #(.width(32)) adder_2 (.a(adder_1_out), .b(F3), .out(adder_2_out));  // open: cin, cout
  // Probe on rt_data
  Adder #(.width(32)) adder_3 (.a(adder_2_out), .b(F4), .out(adder_3_out));  // open: cin, cout
  assign bit_extender_1_out = {{27{1'b0}}, in_2};  // Bit_Extender bit_extender_1
  Adder #(.width(32)) adder_4 (.a(adder_3_out), .b(F5), .out(adder_4_out));  // open: cin, cout
  Multiplier #(.width(32)) multiplier_31 (.a(rt_data), .b(32'h3e8), .out(multiplier_31_out));  // open: cin, cout
  // Probe on bit_extender_1_out
  Adder #(.width(32)) adder_5 (.a(adder_4_out), .b(F6), .out(adder_5_out));  // open: cin, cout
  Divider #(.width(32)) divider_1 (
    .a(multiplier_31_out), .b(bit_extender_1_out), .out(divider_1_out));  // open: upper, rem
  Adder #(.width(32)) adder_6 (.a(adder_5_out), .b(F7), .out(adder_6_out));  // open: cin, cout
  Adder #(.width(32)) adder_7 (.a(adder_6_out), .b(F8), .out(adder_7_out));  // open: cin, cout
  Divider #(.width(32)) divider_2 (.a(divider_1_out), .b(bit_extender_1_out), .out(divider_2_out));  // open: upper, rem
  Divider #(.width(32)) divider_3 (.a(divider_4_out), .b(bit_extender_1_out), .out(divider_3_out));  // open: upper, rem
  Divider #(.width(32)) divider_4 (
    .a(divider_22_out), .b(bit_extender_1_out), .out(divider_4_out));  // open: upper, rem
  Divider #(.width(32)) divider_5 (.a(divider_6_out), .b(bit_extender_1_out), .out(divider_5_out));  // open: upper, rem
  Divider #(.width(32)) divider_6 (
    .a(divider_23_out), .b(bit_extender_1_out), .out(divider_6_out));  // open: upper, rem
  Divider #(.width(32)) divider_7 (
    .a(divider_28_out), .b(bit_extender_1_out), .out(divider_7_out));  // open: upper, rem
  Divider #(.width(32)) divider_8 (.a(divider_7_out), .b(bit_extender_1_out), .out(divider_8_out));  // open: upper, rem
  Adder #(.width(32)) adder_8 (.a(adder_7_out), .b(F9), .out(adder_8_out));  // open: cin, cout
  Divider #(.width(32)) divider_9 (
    .a(divider_10_out), .b(bit_extender_1_out), .out(divider_9_out));  // open: upper, rem
  Divider #(.width(32)) divider_10 (
    .a(divider_2_out), .b(bit_extender_1_out), .out(divider_10_out));  // open: upper, rem
  Divider #(.width(32)) divider_11 (
    .a(divider_12_out), .b(bit_extender_1_out), .out(divider_11_out));  // open: upper, rem
  Divider #(.width(32)) divider_12 (
    .a(divider_3_out), .b(bit_extender_1_out), .out(divider_12_out));  // open: upper, rem
  Divider #(.width(32)) divider_13 (
    .a(divider_14_out), .b(bit_extender_1_out), .out(divider_13_out));  // open: upper, rem
  Divider #(.width(32)) divider_14 (
    .a(divider_5_out), .b(bit_extender_1_out), .out(divider_14_out));  // open: upper, rem
  Divider #(.width(32)) divider_15 (
    .a(divider_8_out), .b(bit_extender_1_out), .out(divider_15_out));  // open: upper, rem
  Divider #(.width(32)) divider_16 (
    .a(divider_15_out), .b(bit_extender_1_out), .out(divider_16_out));  // open: upper, rem
  Adder #(.width(32)) adder_9 (.a(adder_8_out), .b(F10), .out(adder_9_out));  // open: cin, cout
  Divider #(.width(32)) divider_17 (
    .a(divider_18_out), .b(bit_extender_1_out), .out(divider_17_out));  // open: upper, rem
  Divider #(.width(32)) divider_18 (
    .a(divider_9_out), .b(bit_extender_1_out), .out(divider_18_out));  // open: upper, rem
  Divider #(.width(32)) divider_19 (
    .a(divider_11_out), .b(bit_extender_1_out), .out(divider_19_out));  // open: upper, rem
  Divider #(.width(32)) divider_20 (
    .a(divider_13_out), .b(bit_extender_1_out), .out(divider_20_out));  // open: upper, rem
  Divider #(.width(32)) divider_21 (
    .a(divider_16_out), .b(bit_extender_1_out), .out(divider_21_out));  // open: upper, rem
  Adder #(.width(32)) adder_10 (.a(adder_9_out), .b(F11), .out(adder_10_out));  // open: cin, cout
  Adder #(.width(32)) adder_11 (.a(adder_10_out), .b(F12), .out(adder_11_out));  // open: cin, cout
  Divider #(.width(32)) divider_22 (
    .a(divider_17_out), .b(bit_extender_1_out), .out(divider_22_out));  // open: upper, rem
  Divider #(.width(32)) divider_23 (
    .a(divider_19_out), .b(bit_extender_1_out), .out(divider_23_out));  // open: upper, rem
  Divider #(.width(32)) divider_24 (
    .a(divider_20_out), .b(bit_extender_1_out), .out(divider_24_out));  // open: upper, rem
  Divider #(.width(32)) divider_25 (
    .a(divider_24_out), .b(bit_extender_1_out), .out(divider_25_out));  // open: upper, rem
  Divider #(.width(32)) divider_26 (
    .a(divider_21_out), .b(bit_extender_1_out), .out(divider_26_out));  // open: upper, rem
  Divider #(.width(32)) divider_27 (
    .a(divider_26_out), .b(bit_extender_1_out), .out(divider_27_out));  // open: upper, rem
  Multiplier #(.width(32)) multiplier_32 (.a(bit_extender_1_out), .b(32'h3e8), .out(under));  // open: cin, cout
  Divider #(.width(32)) divider_28 (
    .a(divider_25_out), .b(bit_extender_1_out), .out(divider_28_out));  // open: upper, rem
  Divider #(.width(32)) divider_29 (
    .a(divider_27_out), .b(bit_extender_1_out), .out(divider_29_out));  // open: upper, rem
  // Probe on adder_13_out
  // Probe on adder_11_out
  Divider #(.width(32)) divider_30 (
    .a(divider_31_out), .b(bit_extender_1_out), .out(divider_30_out));  // open: upper, rem
  Divider #(.width(32)) divider_31 (
    .a(divider_29_out), .b(bit_extender_1_out), .out(divider_31_out));  // open: upper, rem
  assign bit_extender_2_out = {{27{1'b0}}, adder_13_out};  // Bit_Extender bit_extender_2
  Shifter #(.width(32)) shifter_3 (.in(bit_extender_2_out), .\dist (5'b11011), .out(shifter_3_out));
  Comparator #(.width(32)) comparator_2 (.a(divider_1_out), .b(under), .lt(comparator_2_lt[0]));  // open: gt, eq
  Comparator #(.width(32)) comparator_3 (.a(divider_2_out), .b(under), .lt(comparator_2_lt[1]));  // open: gt, eq
  Comparator #(.width(32)) comparator_4 (.a(divider_10_out), .b(under), .lt(comparator_2_lt[2]));  // open: gt, eq
  Comparator #(.width(32)) comparator_5 (.a(divider_9_out), .b(under), .lt(comparator_2_lt[3]));  // open: gt, eq
  Comparator #(.width(32)) comparator_6 (.a(divider_18_out), .b(under), .lt(comparator_2_lt[4]));  // open: gt, eq
  Comparator #(.width(32)) comparator_7 (.a(divider_17_out), .b(under), .lt(comparator_2_lt[5]));  // open: gt, eq
  Comparator #(.width(32)) comparator_8 (.a(divider_22_out), .b(under), .lt(comparator_2_lt[6]));  // open: gt, eq
  Comparator #(.width(32)) comparator_9 (.a(divider_4_out), .b(under), .lt(comparator_2_lt[7]));  // open: gt, eq
  Comparator #(.width(32)) comparator_10 (.a(divider_3_out), .b(under), .lt(comparator_2_lt[8]));  // open: gt, eq
  Comparator #(.width(32)) comparator_11 (.a(divider_12_out), .b(under), .lt(comparator_2_lt[9]));  // open: gt, eq
  Comparator #(.width(32)) comparator_12 (.a(divider_11_out), .b(under), .lt(comparator_2_lt[10]));  // open: gt, eq
  Comparator #(.width(32)) comparator_13 (.a(divider_19_out), .b(under), .lt(comparator_2_lt[11]));  // open: gt, eq
  Comparator #(.width(32)) comparator_14 (.a(divider_23_out), .b(under), .lt(comparator_2_lt[12]));  // open: gt, eq
  Comparator #(.width(32)) comparator_15 (.a(divider_6_out), .b(under), .lt(comparator_2_lt[13]));  // open: gt, eq
  Comparator #(.width(32)) comparator_16 (.a(divider_5_out), .b(under), .lt(comparator_2_lt[14]));  // open: gt, eq
  Comparator #(.width(32)) comparator_17 (.a(divider_14_out), .b(under), .lt(comparator_2_lt[15]));  // open: gt, eq
  Comparator #(.width(32)) comparator_18 (.a(divider_13_out), .b(under), .lt(comparator_2_lt[16]));  // open: gt, eq
  Comparator #(.width(32)) comparator_19 (.a(divider_20_out), .b(under), .lt(comparator_2_lt[17]));  // open: gt, eq
  Comparator #(.width(32)) comparator_20 (.a(divider_24_out), .b(under), .lt(comparator_2_lt[18]));  // open: gt, eq
  Comparator #(.width(32)) comparator_21 (.a(divider_25_out), .b(under), .lt(comparator_2_lt[19]));  // open: gt, eq
  Comparator #(.width(32)) comparator_22 (.a(divider_28_out), .b(under), .lt(comparator_2_lt[20]));  // open: gt, eq
  Comparator #(.width(32)) comparator_23 (.a(divider_7_out), .b(under), .lt(comparator_2_lt[21]));  // open: gt, eq
  Comparator #(.width(32)) comparator_24 (.a(divider_8_out), .b(under), .lt(comparator_2_lt[22]));  // open: gt, eq
  Comparator #(.width(32)) comparator_25 (.a(divider_15_out), .b(under), .lt(comparator_2_lt[23]));  // open: gt, eq
  Comparator #(.width(32)) comparator_26 (.a(divider_16_out), .b(under), .lt(comparator_2_lt[24]));  // open: gt, eq
  Comparator #(.width(32)) comparator_27 (.a(divider_21_out), .b(under), .lt(comparator_2_lt[25]));  // open: gt, eq
  Comparator #(.width(32)) comparator_28 (.a(divider_26_out), .b(under), .lt(comparator_2_lt[26]));  // open: gt, eq
  Comparator #(.width(32)) comparator_29 (.a(divider_27_out), .b(under), .lt(comparator_2_lt[27]));  // open: gt, eq
  Comparator #(.width(32)) comparator_30 (.a(divider_29_out), .b(under), .lt(comparator_2_lt[28]));  // open: gt, eq
  Comparator #(.width(32)) comparator_31 (.a(divider_31_out), .b(under), .lt(comparator_2_lt[29]));  // open: gt, eq
  Comparator #(.width(32)) comparator_32 (.a(divider_30_out), .b(under), .lt(comparator_2_lt[30]));  // open: gt, eq
  Adder #(.width(32)) adder_12 (.a(shifter_3_out), .b(adder_11_out), .out(log));  // open: cin, cout
  BitAdder #(.width(31)) bitadder_1 (.in0(not_1_out), .out(bitadder_1_out));
  assign not_1_out = ~comparator_2_lt;  // NOT_Gate not_1, 31 bits wide
  Adder #(.width(5)) adder_13 (.a(bitadder_1_out), .b(5'b00001), .out(adder_13_out));  // open: cin, cout
  Multiplexer #(.select(5), .width(32)) multiplexer_4 (
    .in1(divider_1_out), .in2(divider_2_out), .in3(divider_10_out), .in4(divider_9_out),
    .in5(divider_18_out), .in6(divider_17_out), .in7(divider_22_out), .in8(divider_4_out),
    .in9(divider_3_out), .in10(divider_12_out), .in11(divider_11_out), .in12(divider_19_out),
    .in13(divider_23_out), .in14(divider_6_out), .in15(divider_5_out), .in16(divider_14_out),
    .in17(divider_13_out), .in18(divider_20_out), .in19(divider_24_out), .in20(divider_25_out),
    .in21(divider_28_out), .in22(divider_7_out), .in23(divider_8_out), .in24(divider_15_out),
    .in25(divider_16_out), .in26(divider_21_out), .in27(divider_26_out), .in28(divider_27_out),
    .in29(divider_29_out), .in30(divider_31_out), .in31(divider_30_out), .out(multiplexer_4_out),
    .sel(adder_13_out));  // open: in0, en
  Multiplier #(.width(32)) multiplier_33 (
    .a(multiplexer_26_out), .b(multiplexer_26_out), .out(multiplier_33_out));  // open: cin, cout
  Multiplier #(.width(32)) multiplier_34 (
    .a(multiplexer_27_out), .b(multiplexer_27_out), .out(multiplier_34_out));  // open: cin, cout
  Multiplier #(.width(32)) multiplier_35 (
    .a(multiplexer_4_out), .b(multiplexer_4_out), .out(multiplier_35_out));  // open: cin, cout
  Divider #(.width(32)) divider_32 (.a(multiplier_35_out), .b(32'h3e8), .out(divider_32_out));  // open: upper, rem
  Divider #(.width(32)) divider_33 (.a(multiplier_33_out), .b(32'h3e8), .out(divider_33_out));  // open: upper, rem
  Divider #(.width(32)) divider_34 (.a(multiplier_34_out), .b(32'h3e8), .out(divider_34_out));  // open: upper, rem
  Comparator #(.width(32)) comparator_33 (.a(divider_32_out), .b(under), .gt(comparator_33_gt));  // open: eq, lt
  Comparator #(.width(32)) comparator_34 (.a(divider_33_out), .b(under), .gt(comparator_34_gt));  // open: eq, lt
  Comparator #(.width(32)) comparator_35 (.a(divider_34_out), .b(under), .gt(comparator_35_gt));  // open: eq, lt
  Multiplexer #(.width(32)) multiplexer_5 (
    .in0({32{1'b0}}), .in1(32'h1f4), .out(F1), .sel(comparator_33_gt));  // open: en
  Multiplexer #(.width(32)) multiplexer_6 (
    .in0({32{1'b0}}), .in1(divider_63_out), .out(F5), .sel(comparator_34_gt));  // open: en
  Multiplexer #(.width(32)) multiplexer_7 (
    .in0({32{1'b0}}), .in1(divider_65_out), .out(F9), .sel(comparator_35_gt));  // open: en
  Multiplexer #(.width(32)) multiplexer_8 (
    .in0(divider_32_out), .in1(divider_35_out), .out(multiplexer_8_out), .sel(comparator_33_gt));  // open: en
  Divider #(.width(32)) divider_35 (.a(multiplier_35_out), .b(under), .out(divider_35_out));  // open: upper, rem
  Divider #(.width(32)) divider_36 (.a(32'h1f4), .b(32'h2), .out(divider_36_out));  // open: upper, rem
  Multiplexer #(.width(32)) multiplexer_9 (
    .in0(divider_33_out), .in1(divider_37_out), .out(multiplexer_9_out), .sel(comparator_34_gt));  // open: en
  Divider #(.width(32)) divider_37 (.a(multiplier_33_out), .b(under), .out(divider_37_out));  // open: upper, rem
  Divider #(.width(32)) divider_38 (.a(divider_63_out), .b(32'h2), .out(divider_38_out));  // open: upper, rem
  Multiplexer #(.width(32)) multiplexer_10 (
    .in0(divider_34_out), .in1(divider_39_out), .out(multiplexer_10_out), .sel(comparator_35_gt));  // open: en
  Divider #(.width(32)) divider_39 (.a(multiplier_34_out), .b(under), .out(divider_39_out));  // open: upper, rem
  Divider #(.width(32)) divider_40 (.a(divider_65_out), .b(32'h2), .out(divider_40_out));  // open: upper, rem
  Multiplier #(.width(32)) multiplier_36 (
    .a(multiplexer_8_out), .b(multiplexer_8_out), .out(multiplier_36_out));  // open: cin, cout
  Multiplier #(.width(32)) multiplier_37 (
    .a(multiplexer_9_out), .b(multiplexer_9_out), .out(multiplier_37_out));  // open: cin, cout
  Multiplier #(.width(32)) multiplier_38 (
    .a(multiplexer_10_out), .b(multiplexer_10_out), .out(multiplier_38_out));  // open: cin, cout
  Divider #(.width(32)) divider_41 (.a(multiplier_36_out), .b(32'h3e8), .out(divider_41_out));  // open: upper, rem
  Divider #(.width(32)) divider_42 (.a(multiplier_37_out), .b(32'h3e8), .out(divider_42_out));  // open: upper, rem
  Divider #(.width(32)) divider_43 (.a(multiplier_38_out), .b(32'h3e8), .out(divider_43_out));  // open: upper, rem
  Comparator #(.width(32)) comparator_36 (.a(divider_41_out), .b(under), .gt(comparator_36_gt));  // open: eq, lt
  Comparator #(.width(32)) comparator_37 (.a(divider_42_out), .b(under), .gt(comparator_37_gt));  // open: eq, lt
  Comparator #(.width(32)) comparator_38 (.a(divider_43_out), .b(under), .gt(comparator_38_gt));  // open: eq, lt
  Multiplexer #(.width(32)) multiplexer_11 (
    .in0({32{1'b0}}), .in1(divider_36_out), .out(F2), .sel(comparator_36_gt));  // open: en
  Multiplexer #(.width(32)) multiplexer_12 (
    .in0({32{1'b0}}), .in1(divider_38_out), .out(F6), .sel(comparator_37_gt));  // open: en
  Multiplexer #(.width(32)) multiplexer_13 (
    .in0({32{1'b0}}), .in1(divider_40_out), .out(F10), .sel(comparator_38_gt));  // open: en
  Multiplexer #(.width(32)) multiplexer_14 (
    .in0(divider_41_out), .in1(divider_44_out), .out(multiplexer_14_out), .sel(comparator_36_gt));  // open: en
  Divider #(.width(32)) divider_44 (.a(multiplier_36_out), .b(under), .out(divider_44_out));  // open: upper, rem
  Divider #(.width(32)) divider_45 (.a(divider_36_out), .b(32'h2), .out(divider_45_out));  // open: upper, rem
  Multiplexer #(.width(32)) multiplexer_15 (
    .in0(divider_42_out), .in1(divider_46_out), .out(multiplexer_15_out), .sel(comparator_37_gt));  // open: en
  Divider #(.width(32)) divider_46 (.a(multiplier_37_out), .b(under), .out(divider_46_out));  // open: upper, rem
  Divider #(.width(32)) divider_47 (.a(divider_38_out), .b(32'h2), .out(divider_47_out));  // open: upper, rem
  Multiplexer #(.width(32)) multiplexer_16 (
    .in0(divider_43_out), .in1(divider_48_out), .out(multiplexer_16_out), .sel(comparator_38_gt));  // open: en
  Divider #(.width(32)) divider_48 (.a(multiplier_38_out), .b(under), .out(divider_48_out));  // open: upper, rem
  Divider #(.width(32)) divider_49 (.a(divider_40_out), .b(32'h2), .out(divider_49_out));  // open: upper, rem
  Multiplier #(.width(32)) multiplier_39 (
    .a(multiplexer_14_out), .b(multiplexer_14_out), .out(multiplier_39_out));  // open: cin, cout
  Multiplier #(.width(32)) multiplier_40 (
    .a(multiplexer_15_out), .b(multiplexer_15_out), .out(multiplier_40_out));  // open: cin, cout
  Multiplier #(.width(32)) multiplier_41 (
    .a(multiplexer_16_out), .b(multiplexer_16_out), .out(multiplier_41_out));  // open: cin, cout
  Divider #(.width(32)) divider_50 (.a(multiplier_39_out), .b(32'h3e8), .out(divider_50_out));  // open: upper, rem
  Divider #(.width(32)) divider_51 (.a(multiplier_40_out), .b(32'h3e8), .out(divider_51_out));  // open: upper, rem
  Divider #(.width(32)) divider_52 (.a(multiplier_41_out), .b(32'h3e8), .out(divider_52_out));  // open: upper, rem
  Comparator #(.width(32)) comparator_39 (.a(divider_51_out), .b(under), .gt(comparator_39_gt));  // open: eq, lt
  Comparator #(.width(32)) comparator_40 (.a(divider_52_out), .b(under), .gt(comparator_40_gt));  // open: eq, lt
  Comparator #(.width(32)) comparator_41 (.a(divider_50_out), .b(under), .gt(comparator_41_gt));  // open: eq, lt
  Multiplexer #(.width(32)) multiplexer_17 (
    .in0({32{1'b0}}), .in1(divider_45_out), .out(F3), .sel(comparator_41_gt));  // open: en
  Multiplexer #(.width(32)) multiplexer_18 (
    .in0({32{1'b0}}), .in1(divider_47_out), .out(F7), .sel(comparator_39_gt));  // open: en
  Multiplexer #(.width(32)) multiplexer_19 (
    .in0({32{1'b0}}), .in1(divider_49_out), .out(F11), .sel(comparator_40_gt));  // open: en
  Divider #(.width(32)) divider_53 (.a(multiplier_39_out), .b(under), .out(divider_53_out));  // open: upper, rem
  Divider #(.width(32)) divider_54 (.a(divider_45_out), .b(32'h2), .out(divider_54_out));  // open: upper, rem
  Multiplexer #(.width(32)) multiplexer_20 (
    .in0(divider_51_out), .in1(divider_55_out), .out(multiplexer_20_out), .sel(comparator_39_gt));  // open: en
  Divider #(.width(32)) divider_55 (.a(multiplier_40_out), .b(under), .out(divider_55_out));  // open: upper, rem
  Divider #(.width(32)) divider_56 (.a(divider_47_out), .b(32'h2), .out(divider_56_out));  // open: upper, rem
  Multiplexer #(.width(32)) multiplexer_21 (
    .in0(divider_52_out), .in1(divider_57_out), .out(multiplexer_21_out), .sel(comparator_40_gt));  // open: en
  Divider #(.width(32)) divider_57 (.a(multiplier_41_out), .b(under), .out(divider_57_out));  // open: upper, rem
  Divider #(.width(32)) divider_58 (.a(divider_49_out), .b(32'h2), .out(divider_58_out));  // open: upper, rem
  Multiplexer #(.width(32)) multiplexer_22 (
    .in0(divider_50_out), .in1(divider_53_out), .out(multiplexer_22_out), .sel(comparator_41_gt));  // open: en
  Multiplier #(.width(32)) multiplier_42 (
    .a(multiplexer_22_out), .b(multiplexer_22_out), .out(multiplier_42_out));  // open: cin, cout
  Multiplier #(.width(32)) multiplier_43 (
    .a(multiplexer_20_out), .b(multiplexer_20_out), .out(multiplier_43_out));  // open: cin, cout
  Multiplier #(.width(32)) multiplier_44 (
    .a(multiplexer_21_out), .b(multiplexer_21_out), .out(multiplier_44_out));  // open: cin, cout
  Divider #(.width(32)) divider_59 (.a(multiplier_42_out), .b(32'h3e8), .out(divider_59_out));  // open: upper, rem
  Divider #(.width(32)) divider_60 (.a(multiplier_43_out), .b(32'h3e8), .out(divider_60_out));  // open: upper, rem
  Divider #(.width(32)) divider_61 (.a(multiplier_44_out), .b(32'h3e8), .out(divider_61_out));  // open: upper, rem
  Comparator #(.width(32)) comparator_42 (.a(divider_59_out), .b(under), .gt(comparator_42_gt));  // open: eq, lt
  Comparator #(.width(32)) comparator_43 (.a(divider_60_out), .b(under), .gt(comparator_43_gt));  // open: eq, lt
  Comparator #(.width(32)) comparator_44 (.a(divider_61_out), .b(under), .gt(comparator_44_gt));  // open: eq, lt
  Multiplexer #(.width(32)) multiplexer_23 (
    .in0({32{1'b0}}), .in1(divider_54_out), .out(F4), .sel(comparator_42_gt));  // open: en
  Multiplexer #(.width(32)) multiplexer_24 (
    .in0({32{1'b0}}), .in1(divider_56_out), .out(F8), .sel(comparator_43_gt));  // open: en
  Multiplexer #(.width(32)) multiplexer_25 (
    .in0({32{1'b0}}), .in1(divider_58_out), .out(F12), .sel(comparator_44_gt));  // open: en
  Multiplexer #(.width(32)) multiplexer_26 (
    .in0(divider_59_out), .in1(divider_62_out), .out(multiplexer_26_out), .sel(comparator_42_gt));  // open: en
  Divider #(.width(32)) divider_62 (.a(multiplier_42_out), .b(under), .out(divider_62_out));  // open: upper, rem
  Divider #(.width(32)) divider_63 (.a(divider_54_out), .b(32'h2), .out(divider_63_out));  // open: upper, rem
  Multiplexer #(.width(32)) multiplexer_27 (
    .in0(divider_60_out), .in1(divider_64_out), .out(multiplexer_27_out), .sel(comparator_43_gt));  // open: en
  Divider #(.width(32)) divider_64 (.a(multiplier_43_out), .b(under), .out(divider_64_out));  // open: upper, rem
  Divider #(.width(32)) divider_65 (.a(divider_56_out), .b(32'h2), .out(divider_65_out));  // open: upper, rem
  Multiplexer #(.width(32)) multiplexer_28 (
    .in0(divider_61_out), .in1(divider_66_out), .sel(comparator_44_gt));  // open: out, en
  Divider #(.width(32)) divider_66 (.a(multiplier_44_out), .b(under), .out(divider_66_out));  // open: upper, rem
  Divider #(.width(32)) divider_67 (.a(divider_58_out), .b(32'h2));  // open: out, upper, rem

  // Other names for the same wires on the sheet: shamt[4:0] = in_2
endmodule
