// Logisim project 3_Data_memory.circ as structural Verilog: 1 circuit, main circuit main
module main (
  input  [23:0] input_address,
  input  CLK,
  input  Write_EN,
  input  [31:0] input_data,
  output [31:0] output_data
);

  wire not_1_out;

  not not_1 (not_1_out, Write_EN);
  assign output_data = Write_EN ? input_data : 32'bz;  // Controlled_Buffer controlled_buffer_1
  RAM #(.addrWidth(24), .dataWidth(32)) ram_1 (
    .addr(input_address), .data(output_data), .clk(CLK), .ld(not_1_out));  // open: sel, clr
endmodule
